// Logisim project projeto.circ as structural Verilog: 9 circuits, main circuit addregs
module addregs (
  input  [15:0] ftes,
  input  [15:0] space,
  output [15:0] fates
);

  Adder #(.width(16)) adder_1 (.a(ftes), .b(space), .out(fates));  // open: cin, cout
endmodule

module litoreg (
  input  [8:0] colosso,
  output [15:0] fates
);

  assign fates = {{7{colosso[8]}}, colosso};  // Bit_Extender bit_extender_1
endmodule

module dot (
  input  [15:0] ftes,
  input  [15:0] space,
  input  [15:0] fatesone,
  input  [15:0] spaceone,
  output [15:0] fates
);

  wire [15:0] multiplier_1_out, multiplier_2_out;

  Multiplier #(.width(16)) multiplier_1 (.a(ftes), .b(space), .out(multiplier_1_out));  // open: cin, cout
  Multiplier #(.width(16)) multiplier_2 (.a(fatesone), .b(spaceone), .out(multiplier_2_out));  // open: cin, cout
  Adder #(.width(16)) adder_1 (.a(multiplier_1_out), .b(multiplier_2_out), .out(fates));  // open: cin, cout
endmodule

module dota (
  input  [15:0] ftes,
  input  [15:0] space,
  input  [15:0] back,
  input  [15:0] spaceone,
  input  [15:0] backone,
  output [15:0] fates
);

  wire [15:0] adder_1_out, multiplier_1_out, multiplier_2_out;

  Multiplier #(.width(16)) multiplier_1 (.a(space), .b(back), .out(multiplier_1_out));  // open: cin, cout
  Multiplier #(.width(16)) multiplier_2 (.a(spaceone), .b(backone), .out(multiplier_2_out));  // open: cin, cout
  Adder #(.width(16)) adder_1 (.a(multiplier_1_out), .b(multiplier_2_out), .out(adder_1_out));  // open: cin, cout
  Adder #(.width(16)) adder_2 (.a(ftes), .b(adder_1_out), .out(fates));  // open: cin, cout
endmodule

module cpu (
);

  wire button_1_out, clock_1_out;
  wire [15:0] alu_1_data, pcounter_1_pc, regbank_1_back, regbank_1_backone, regbank_1_fates,
       regbank_1_fatesone, regbank_1_space, regbank_1_spaceone, rom_1_data;

  Clock clock_1 (.out(clock_1_out));
  Button button_1 (.out(button_1_out));
  pcounter pcounter_1 (.clock(clock_1_out), .reset(button_1_out), .pc(pcounter_1_pc));
  ROM #(.addrWidth(16), .dataWidth(16)) rom_1 (.addr(pcounter_1_pc), .data(rom_1_data));
  regbank regbank_1 (
    .data(alu_1_data), .clock(clock_1_out), .selfates(rom_1_data[6:4]), .selspace(rom_1_data[12:10]),
    .selback(rom_1_data[15:13]), .space(regbank_1_space), .back(regbank_1_back), .fates(regbank_1_fates),
    .spaceone(regbank_1_spaceone), .backone(regbank_1_backone), .fatesone(regbank_1_fatesone));
  alu alu_1 (
    .colosso(rom_1_data[15:7]), .space(regbank_1_space), .fates(regbank_1_fates),
    .fatesone(regbank_1_fatesone), .spaceone(regbank_1_spaceone), .dna(rom_1_data[3:0]),
    .back(regbank_1_back), .backone(regbank_1_backone), .data(alu_1_data));

  // Notes on the sheet:
  //   contents of rom_1 (hex, n*v repeats v):
  //   101 191 221 131 c1 2d1 161 171 432 803 d004
endmodule

module pcounter (
  input  clock,
  input  reset,
  output [15:0] pc
);

  wire [15:0] adder_1_out;

  Adder #(.width(16)) adder_1 (.a(pc), .b({16{1'b0}}), .out(adder_1_out), .cin(1'b1));  // open: cout
  Register #(.width(16)) register_1 (.D(adder_1_out), .en(1'b1), .clk(clock), .Q(pc), .clr(reset));
endmodule

module regbank (
  input  [15:0] data,
  input  clock,
  input  [2:0] selfates,
  input  [2:0] selspace,
  input  [2:0] selback,
  output [15:0] space,
  output [15:0] back,
  output [15:0] fates,
  output [15:0] spaceone,
  output [15:0] backone,
  output [15:0] fatesone
);

  wire decoder_1_out0, decoder_1_out1, decoder_1_out2, decoder_1_out3, decoder_1_out4, decoder_1_out5,
       decoder_1_out6, decoder_1_out7;
  wire [2:0] adder_1_out, adder_2_out, adder_3_out;
  wire [15:0] r0_q, r1_q, r2_q, r3_q, r4_q, r5_q, r6_q, r7_q;

  Adder #(.width(3)) adder_1 (.a(selfates), .b(3'b001), .out(adder_1_out));  // open: cin, cout
  Adder #(.width(3)) adder_2 (.a(selspace), .b(3'b001), .out(adder_2_out));  // open: cin, cout
  Register #(.width(16)) r0 (.D(data), .en(decoder_1_out0), .clk(clock), .Q(r0_q));  // open: clr
  Decoder #(.select(3)) decoder_1 (
    .out0(decoder_1_out0), .out1(decoder_1_out1), .out2(decoder_1_out2), .out3(decoder_1_out3),
    .out4(decoder_1_out4), .out5(decoder_1_out5), .out6(decoder_1_out6), .out7(decoder_1_out7), .sel(selfates));  // open: en
  Adder #(.width(3)) adder_3 (.a(selback), .b(3'b001), .out(adder_3_out));  // open: cin, cout
  Register #(.width(16)) r1 (.D(data), .en(decoder_1_out1), .clk(clock), .Q(r1_q));  // open: clr
  Register #(.width(16)) r2 (.D(data), .en(decoder_1_out2), .clk(clock), .Q(r2_q));  // open: clr
  Register #(.width(16)) r3 (.D(data), .en(decoder_1_out3), .clk(clock), .Q(r3_q));  // open: clr
  Register #(.width(16)) r4 (.D(data), .en(decoder_1_out4), .clk(clock), .Q(r4_q));  // open: clr
  Register #(.width(16)) r5 (.D(data), .en(decoder_1_out5), .clk(clock), .Q(r5_q));  // open: clr
  Register #(.width(16)) r6 (.D(data), .en(decoder_1_out6), .clk(clock), .Q(r6_q));  // open: clr
  Register #(.width(16)) r7 (.D(data), .en(decoder_1_out7), .clk(clock), .Q(r7_q));  // open: clr
  Multiplexer #(.select(3), .width(16)) multiplexer_1 (
    .in0(r0_q), .in1(r1_q), .in2(r2_q), .in3(r3_q), .in4(r4_q), .in5(r5_q), .in6(r6_q), .in7(r7_q),
    .out(spaceone), .sel(adder_2_out));
  Multiplexer #(.select(3), .width(16)) multiplexer_2 (
    .in0(r0_q), .in1(r1_q), .in2(r2_q), .in3(r3_q), .in4(r4_q), .in5(r5_q), .in6(r6_q), .in7(r7_q),
    .out(backone), .sel(adder_3_out));
  Multiplexer #(.select(3), .width(16)) multiplexer_3 (
    .in0(r0_q), .in1(r1_q), .in2(r2_q), .in3(r3_q), .in4(r4_q), .in5(r5_q), .in6(r6_q), .in7(r7_q),
    .out(fatesone), .sel(adder_1_out));
  Multiplexer #(.select(3), .width(16)) multiplexer_4 (
    .in0(r0_q), .in1(r1_q), .in2(r2_q), .in3(r3_q), .in4(r4_q), .in5(r5_q), .in6(r6_q), .in7(r7_q),
    .out(space), .sel(selspace));
  Multiplexer #(.select(3), .width(16)) multiplexer_5 (
    .in0(r0_q), .in1(r1_q), .in2(r2_q), .in3(r3_q), .in4(r4_q), .in5(r5_q), .in6(r6_q), .in7(r7_q),
    .out(back), .sel(selback));
  Multiplexer #(.select(3), .width(16)) multiplexer_6 (
    .in0(r0_q), .in1(r1_q), .in2(r2_q), .in3(r3_q), .in4(r4_q), .in5(r5_q), .in6(r6_q), .in7(r7_q),
    .out(fates), .sel(selfates));
endmodule

module alu (
  input  [8:0] colosso,
  input  [15:0] space,
  input  [15:0] fates,
  input  [15:0] fatesone,
  input  [15:0] spaceone,
  input  [3:0] dna,
  input  [15:0] back,
  input  [15:0] backone,
  output [15:0] data
);

  wire [15:0] addregs_1_fates, dot_1_fates, dota_1_fates, litoreg_1_fates, sub_1_fates;

  litoreg litoreg_1 (.colosso(colosso), .fates(litoreg_1_fates));
  addregs addregs_1 (.ftes(fates), .space(space), .fates(addregs_1_fates));
  dot dot_1 (.ftes(fates), .space(space), .fatesone(fatesone), .spaceone(spaceone), .fates(dot_1_fates));
  dota dota_1 (.ftes(fates), .space(space), .back(back), .spaceone(spaceone), .backone(backone), .fates(dota_1_fates));
  sub sub_1 (.ftes(fates), .space(space), .fates(sub_1_fates));
  Multiplexer #(.select(4), .width(16)) multiplexer_1 (
    .in0(fates), .in1(litoreg_1_fates), .in2(addregs_1_fates), .in3(dot_1_fates), .in4(dota_1_fates),
    .in5(sub_1_fates), .out(data), .sel(dna));  // open: in6, in7, in8, in9, in10, in11, in12, in13, in14, in15
endmodule

module sub (
  input  [15:0] ftes,
  input  [15:0] space,
  output [15:0] fates
);

  Subtractor #(.width(16)) subtractor_1 (.a(ftes), .b(space), .out(fates));  // open: bin, bout
endmodule
